// Digital circuit diglab_02_03-fulladder-sop.dig as structural Verilog
module diglab_02_03_fulladder_sop (
  input  A,
  input  B,
  input  Cin,
  output Sum,
  output Cout
);

  wire a_t, and_1_out, and_2_out, and_3_out, and_4_out, and_5_out, and_6_out, and_7_out, b_t, c_t;

  not not_1 (a_t, A);
  not not_2 (b_t, B);
  not not_3 (c_t, Cin);
  and and_1 (and_1_out, a_t, b_t, Cin);
  and and_2 (and_2_out, a_t, B, c_t);
  and and_3 (and_3_out, A, b_t, c_t);
  and and_4 (and_4_out, A, B, Cin);
  and and_5 (and_5_out, a_t, B, Cin);
  and and_6 (and_6_out, A, b_t, Cin);
  and and_7 (and_7_out, A, B, c_t);
  or or_1 (Sum, and_1_out, and_2_out, and_3_out, and_4_out);
  or or_2 (Cout, and_4_out, and_5_out, and_6_out, and_7_out);

  // Other names for the same wires on the sheet: c = Cin
endmodule
