// Digital circuit diglab_08_05-moore-single-pulser.dig as structural Verilog
module diglab_08_05_moore_single_pulser (
  input  P,
  input  Clr,
  input  clock,
  output Z
);

  wire and_1_out, d_ff_1_nq, d_ff_2_q, d_ff_3_q, not_1_out;

  not not_1 (not_1_out, Clr);
  and and_1 (and_1_out, P, not_1_out);
  D_FF d_ff_1 (.D(and_1_out), .C(clock), .nQ(d_ff_1_nq));  // open: Q
  D_FF d_ff_2 (.D(and_1_out), .C(clock), .Q(d_ff_2_q));  // open: nQ
  D_FF d_ff_3 (.D(d_ff_1_nq), .C(clock), .Q(d_ff_3_q));  // open: nQ
  and and_2 (Z, d_ff_2_q, d_ff_3_q);
endmodule
