// Digital circuit diglab_09_01-vending-machine.dig as structural Verilog
module diglab_09_01_vending_machine (
  input  P5,
  input  reset,
  input  clock,
  input  P10,
  input  P20,
  input  Pcoffee,
  input  Ptea,
  input  Pchange,
  input  Pnext,
  output [5:0] Balance,
  output CoffeeOut,
  output TeaOut,
  output [1:0] Change5,
  output [1:0] Change10,
  output [1:0] Change20
);

  wire and_9_out, and_10_out, and_11_out, and_12_out, and_13_out, and_14_out, and_15_out, comparator_1_gt,
       comparator_2_gt, comparator_3_gt, comparator_4_lt, comparator_5_lt, d_ff_1_nq, d_ff_2_nq, d_ff_3_nq,
       d_ff_4_nq, d_ff_5_nq, d_ff_6_nq, d_ff_7_nq, d_ff_8_nq, d_ff_9_q, d_ff_10_q, d_ff_11_q, d_ff_12_q,
       d_ff_13_q, d_ff_14_q, d_ff_15_q, d_ff_16_q, d_ff_17_q, d_ff_18_q, d_ff_19_q, d_ff_20_q, d_ff_21_q,
       d_ff_22_q, d_ff_23_q, d_ff_24_q, multiplexer_13_out, multiplexer_14_out, nor_1_out, not_1_out,
       not_2_out, not_3_out, not_4_out, not_5_out, not_6_out, not_7_out, not_8_out, not_9_out, or_1_out,
       or_2_out, or_3_out, or_4_out, p5_t, p10_t, p20_t, pChange_t, pCoffee_t, pNext_t, pTea_t, reset_t;
  wire [1:0] div_1_q, div_2_q, div_3_q, multiplexer_5_out, multiplexer_6_out, multiplexer_7_out,
       multiplexer_8_out, multiplexer_9_out, multiplexer_10_out;
  wire [5:0] add_1_s, div_1_r, div_2_r, multiplexer_1_out, multiplexer_2_out, multiplexer_3_out,
       multiplexer_4_out, multiplexer_11_out, multiplexer_12_out, multiplexer_15_out;
  wire [5:2] div_1_q_2, div_2_q_2, div_3_q_2;

  D_FF d_ff_1 (.D(reset), .C(clock), .nQ(d_ff_1_nq));  // open: Q
  D_FF d_ff_2 (.D(P5), .C(clock), .nQ(d_ff_2_nq));  // open: Q
  D_FF d_ff_3 (.D(P10), .C(clock), .nQ(d_ff_3_nq));  // open: Q
  D_FF d_ff_4 (.D(P20), .C(clock), .nQ(d_ff_4_nq));  // open: Q
  D_FF d_ff_5 (.D(Pcoffee), .C(clock), .nQ(d_ff_5_nq));  // open: Q
  D_FF d_ff_6 (.D(Ptea), .C(clock), .nQ(d_ff_6_nq));  // open: Q
  D_FF d_ff_7 (.D(Pchange), .C(clock), .nQ(d_ff_7_nq));  // open: Q
  D_FF d_ff_8 (.D(Pnext), .C(clock), .nQ(d_ff_8_nq));  // open: Q
  D_FF d_ff_9 (.D(reset), .C(clock), .Q(d_ff_9_q));  // open: nQ
  D_FF d_ff_10 (.D(d_ff_1_nq), .C(clock), .Q(d_ff_10_q));  // open: nQ
  D_FF d_ff_11 (.D(P5), .C(clock), .Q(d_ff_11_q));  // open: nQ
  D_FF d_ff_12 (.D(d_ff_2_nq), .C(clock), .Q(d_ff_12_q));  // open: nQ
  D_FF d_ff_13 (.D(P10), .C(clock), .Q(d_ff_13_q));  // open: nQ
  D_FF d_ff_14 (.D(d_ff_3_nq), .C(clock), .Q(d_ff_14_q));  // open: nQ
  D_FF d_ff_15 (.D(P20), .C(clock), .Q(d_ff_15_q));  // open: nQ
  D_FF d_ff_16 (.D(d_ff_4_nq), .C(clock), .Q(d_ff_16_q));  // open: nQ
  D_FF d_ff_17 (.D(Pcoffee), .C(clock), .Q(d_ff_17_q));  // open: nQ
  D_FF d_ff_18 (.D(d_ff_5_nq), .C(clock), .Q(d_ff_18_q));  // open: nQ
  D_FF d_ff_19 (.D(Ptea), .C(clock), .Q(d_ff_19_q));  // open: nQ
  D_FF d_ff_20 (.D(d_ff_6_nq), .C(clock), .Q(d_ff_20_q));  // open: nQ
  D_FF d_ff_21 (.D(Pchange), .C(clock), .Q(d_ff_21_q));  // open: nQ
  D_FF d_ff_22 (.D(d_ff_7_nq), .C(clock), .Q(d_ff_22_q));  // open: nQ
  D_FF d_ff_23 (.D(Pnext), .C(clock), .Q(d_ff_23_q));  // open: nQ
  D_FF d_ff_24 (.D(d_ff_8_nq), .C(clock), .Q(d_ff_24_q));  // open: nQ
  and and_1 (reset_t, d_ff_9_q, d_ff_10_q);
  and and_2 (p5_t, d_ff_11_q, d_ff_12_q);
  and and_3 (p10_t, d_ff_13_q, d_ff_14_q);
  and and_4 (p20_t, d_ff_15_q, d_ff_16_q);
  and and_5 (pCoffee_t, d_ff_17_q, d_ff_18_q);
  and and_6 (pTea_t, d_ff_19_q, d_ff_20_q);
  and and_7 (pChange_t, d_ff_21_q, d_ff_22_q);
  and and_8 (pNext_t, d_ff_23_q, d_ff_24_q);
  Comparator #(.Bits(6)) comparator_1 (.a(Balance), .b(6'b101101), .gt(comparator_1_gt));  // open: eq, lt
  Comparator #(.Bits(6)) comparator_2 (.a(Balance), .b(6'b101000), .gt(comparator_2_gt));  // open: eq, lt
  Comparator #(.Bits(6)) comparator_3 (.a(Balance), .b(6'b011110), .gt(comparator_3_gt));  // open: eq, lt
  Comparator #(.Bits(6)) comparator_4 (.a(Balance), .b(6'b011001), .lt(comparator_4_lt));  // open: gt, eq
  Comparator #(.Bits(6)) comparator_5 (.a(Balance), .b(6'b010100), .lt(comparator_5_lt));  // open: gt, eq
  not not_1 (not_1_out, comparator_1_gt);
  not not_2 (not_2_out, comparator_2_gt);
  not not_3 (not_3_out, comparator_3_gt);
  not not_4 (not_4_out, comparator_4_lt);
  not not_5 (not_5_out, CoffeeOut);
  not not_6 (not_6_out, TeaOut);
  not not_7 (not_7_out, comparator_5_lt);
  not not_8 (not_8_out, CoffeeOut);
  not not_9 (not_9_out, TeaOut);
  and and_9 (and_9_out, p5_t, not_1_out);
  and and_10 (and_10_out, p10_t, not_2_out);
  and and_11 (and_11_out, p20_t, not_3_out);
  and and_12 (and_12_out, pCoffee_t, not_4_out, not_5_out, not_6_out);
  and and_13 (and_13_out, pTea_t, not_7_out, not_8_out, not_9_out);
  Div #(.Bits(6)) div_1 (.a(Balance), .b(6'b010100), .q({div_1_q_2, div_1_q}), .r(div_1_r));
  Div #(.Bits(6)) div_2 (.a(div_1_r), .b(6'b001010), .q({div_2_q_2, div_2_q}), .r(div_2_r));
  Div #(.Bits(6)) div_3 (.a(div_2_r), .b(6'b000101), .q({div_3_q_2, div_3_q}));  // open: r
  Multiplexer #(.Bits(6)) multiplexer_1 (.sel(and_9_out), .in_0({6{1'b0}}), .in_1(6'b000101), .out(multiplexer_1_out));
  Multiplexer #(.Bits(6)) multiplexer_2 (
    .sel(and_10_out), .in_0(multiplexer_1_out), .in_1(6'b001010), .out(multiplexer_2_out));
  Multiplexer #(.Bits(6)) multiplexer_3 (
    .sel(and_11_out), .in_0(multiplexer_2_out), .in_1(6'b010100), .out(multiplexer_3_out));
  Multiplexer #(.Bits(6)) multiplexer_4 (
    .sel(and_12_out), .in_0(multiplexer_3_out), .in_1(6'b100111), .out(multiplexer_4_out));
  Multiplexer #(.Bits(2)) multiplexer_5 (.sel(pChange_t), .in_0(Change20), .in_1(div_1_q), .out(multiplexer_5_out));
  Multiplexer #(.Bits(2)) multiplexer_6 (
    .sel(reset_t), .in_0(multiplexer_5_out), .in_1(2'b00), .out(multiplexer_6_out));
  Multiplexer #(.Bits(2)) multiplexer_7 (.sel(pChange_t), .in_0(Change10), .in_1(div_2_q), .out(multiplexer_7_out));
  Multiplexer #(.Bits(2)) multiplexer_8 (
    .sel(reset_t), .in_0(multiplexer_7_out), .in_1(2'b00), .out(multiplexer_8_out));
  Multiplexer #(.Bits(2)) multiplexer_9 (.sel(pChange_t), .in_0(Change5), .in_1(div_3_q), .out(multiplexer_9_out));
  Multiplexer #(.Bits(2)) multiplexer_10 (
    .sel(reset_t), .in_0(multiplexer_9_out), .in_1(2'b00), .out(multiplexer_10_out));
  Multiplexer #(.Bits(6)) multiplexer_11 (
    .sel(and_13_out), .in_0(multiplexer_4_out), .in_1(6'b101100), .out(multiplexer_11_out));
  Multiplexer #(.Bits(6)) multiplexer_12 (
    .sel(or_4_out), .in_0(multiplexer_11_out), .in_1({6{1'b0}}), .out(multiplexer_12_out));
  or or_1 (or_1_out, and_12_out, CoffeeOut);
  or or_2 (or_2_out, and_13_out, TeaOut);
  nor nor_1 (nor_1_out, pNext_t, pChange_t);
  D_FF #(.Bits(2)) u_change20 (.D(multiplexer_6_out), .C(clock), .Q(Change20));  // open: nQ
  D_FF #(.Bits(2)) u_change10 (.D(multiplexer_8_out), .C(clock), .Q(Change10));  // open: nQ
  D_FF #(.Bits(2)) u_change5 (.D(multiplexer_10_out), .C(clock), .Q(Change5));  // open: nQ
  and and_14 (and_14_out, or_1_out, nor_1_out);
  and and_15 (and_15_out, or_2_out, nor_1_out);
  Add #(.Bits(6)) add_1 (.a(multiplexer_12_out), .b(Balance), .c_i(1'b0), .s(add_1_s));  // open: c_o
  or or_3 (or_3_out, reset_t, pChange_t);
  or or_4 (or_4_out, CoffeeOut, TeaOut);
  Multiplexer multiplexer_13 (.sel(reset_t), .in_0(and_14_out), .in_1(1'b0), .out(multiplexer_13_out));
  Multiplexer multiplexer_14 (.sel(reset_t), .in_0(and_15_out), .in_1(1'b0), .out(multiplexer_14_out));
  Multiplexer #(.Bits(6)) multiplexer_15 (.sel(or_3_out), .in_0(add_1_s), .in_1({6{1'b0}}), .out(multiplexer_15_out));
  D_FF u_CoffeeOut (.D(multiplexer_13_out), .C(clock), .Q(CoffeeOut));  // open: nQ
  D_FF u_TeaOut (.D(multiplexer_14_out), .C(clock), .Q(TeaOut));  // open: nQ
  D_FF #(.Bits(6)) u_Balance (.D(multiplexer_15_out), .C(clock), .Q(Balance));  // open: nQ
endmodule
