// Digital circuit diglab_02_01-xor-sop.dig as structural Verilog
module diglab_02_01_xor_sop (
  input  A,
  input  B,
  output Output
);

  wire and_1_out, and_2_out, not_1_out, not_2_out;

  not not_1 (not_1_out, A);
  not not_2 (not_2_out, B);
  and and_1 (and_1_out, not_1_out, B);
  and and_2 (and_2_out, not_2_out, A);
  or or_1 (Output, and_1_out, and_2_out);
endmodule
