// Digital circuit diglab_02_04-fulladder-pos.dig as structural Verilog
module diglab_02_04_fulladder_pos (
  input  A,
  input  B,
  input  Cin,
  output Sum,
  output Cout
);

  wire a_t, b_t, c_t, or_1_out, or_2_out, or_3_out, or_4_out, or_5_out, or_6_out, or_7_out, or_8_out;

  not not_1 (a_t, A);
  not not_2 (b_t, B);
  not not_3 (c_t, Cin);
  or or_1 (or_1_out, A, B, Cin);
  or or_2 (or_2_out, A, b_t, c_t);
  or or_3 (or_3_out, a_t, B, c_t);
  or or_4 (or_4_out, a_t, b_t, Cin);
  or or_5 (or_5_out, A, B, c_t);
  or or_6 (or_6_out, A, b_t, Cin);
  or or_7 (or_7_out, a_t, B, Cin);
  and and_1 (Sum, or_1_out, or_2_out, or_3_out, or_4_out);
  or or_8 (or_8_out, A, B, Cin);
  and and_2 (Cout, or_8_out, or_5_out, or_6_out, or_7_out);

  // Other names for the same wires on the sheet: c = Cin
endmodule
