// Digital circuit diglab_02_07-multiplexer-sop.dig as structural Verilog
module diglab_02_07_multiplexer_sop (
  input  X0,
  input  X1,
  input  Selector,
  output Z
);

  wire and_1_out, and_2_out, not_1_out;

  not not_1 (not_1_out, Selector);
  and and_1 (and_1_out, X1, Selector);
  and and_2 (and_2_out, X0, not_1_out);
  or or_1 (Z, and_1_out, and_2_out);
endmodule
