// Digital circuit diglab_02_08-multiplexer-pos.dig as structural Verilog
module diglab_02_08_multiplexer_pos (
  input  X0,
  input  X1,
  input  Selector,
  output Z
);

  wire not_1_out, or_1_out, or_2_out;

  not not_1 (not_1_out, Selector);
  or or_1 (or_1_out, X0, Selector);
  or or_2 (or_2_out, X1, not_1_out);
  and and_1 (Z, or_1_out, or_2_out);
endmodule
