// Digital circuit diglab_06.dig as structural Verilog
module diglab_06 (
  input  [3:0] A,
  input  [3:0] B,
  input  [2:0] S,
  input  M,
  input  C,
  output [3:0] F,
  output Cout
);

  wire add_1_c_o, add_2_c_o, add_3_c_o, not_3_out, sub_1_c_o, sub_2_c_o, sub_3_c_o;
  wire [3:0] add_1_s, add_2_s, add_3_s, and_1_out, and_2_out, barrelshifter_1_out, barrelshifter_2_out,
       multiplexer_1_out, multiplexer_2_out, nand_1_out, nor_1_out, not_1_out, not_2_out, or_1_out, sub_1_s,
       sub_2_s, sub_3_s, xnor_1_out;

  assign not_1_out = ~A;  // Not not_1, 4 bits wide
  assign not_2_out = ~B;  // Not not_2, 4 bits wide
  not not_3 (not_3_out, C);
  assign nand_1_out = ~(A & B);  // NAnd nand_1, 4 bits wide
  assign nor_1_out = ~(A | B);  // NOr nor_1, 4 bits wide
  assign xnor_1_out = ~(A ^ B);  // XNOr xnor_1, 4 bits wide
  assign and_1_out = A & B;  // And and_1, 4 bits wide
  assign or_1_out = A | B;  // Or or_1, 4 bits wide
  assign and_2_out = A & not_2_out;  // And and_2, 4 bits wide
  Add #(.Bits(4)) add_1 (.a(A), .b(4'b0000), .c_i(C), .s(add_1_s), .c_o(add_1_c_o));
  Sub #(.Bits(4)) sub_1 (.a(A), .b(4'b0000), .c_i(not_3_out), .s(sub_1_s), .c_o(sub_1_c_o));
  Add #(.Bits(4)) add_2 (.a(A), .b(B), .c_i(C), .s(add_2_s), .c_o(add_2_c_o));
  Sub #(.Bits(4)) sub_2 (.a(A), .b(B), .c_i(not_3_out), .s(sub_2_s), .c_o(sub_2_c_o));
  Sub #(.Bits(4)) sub_3 (.a(4'b0000), .b(A), .c_i(not_3_out), .s(sub_3_s), .c_o(sub_3_c_o));
  Add #(.Bits(4)) add_3 (.a(4'b0000), .b(B), .c_i(C), .s(add_3_s), .c_o(add_3_c_o));
  BarrelShifter #(.Bits(4)) barrelshifter_1 (.in(A), .shift(3'b001), .out(barrelshifter_1_out));
  BarrelShifter #(.Bits(4), .direction("right")) barrelshifter_2 (.in(A), .shift(3'b001), .out(barrelshifter_2_out));
  Multiplexer #(.Selector_Bits(3), .Bits(4)) multiplexer_1 (
    .sel(S), .in_0(not_1_out), .in_1(nand_1_out), .in_2(nor_1_out), .in_3(xnor_1_out), .in_4(and_1_out),
    .in_5(or_1_out), .in_6(and_2_out), .in_7(A), .out(multiplexer_1_out));
  Multiplexer #(.Selector_Bits(3), .Bits(4)) multiplexer_2 (
    .sel(S), .in_0(add_1_s), .in_1(sub_1_s), .in_2(add_2_s), .in_3(sub_2_s), .in_4(sub_3_s), .in_5(add_3_s),
    .in_6(barrelshifter_1_out), .in_7(barrelshifter_2_out), .out(multiplexer_2_out));
  Multiplexer #(.Bits(4)) multiplexer_3 (.sel(M), .in_0(multiplexer_1_out), .in_1(multiplexer_2_out), .out(F));
  Multiplexer #(.Selector_Bits(3)) multiplexer_4 (
    .sel(S), .in_0(add_1_c_o), .in_1(sub_1_c_o), .in_2(add_2_c_o), .in_3(sub_2_c_o), .in_4(sub_3_c_o),
    .in_5(add_3_c_o), .in_6(1'b0), .in_7(1'b0), .out(Cout));
endmodule
