// Digital circuit diglab_final_02-any-root.dig as structural Verilog
module diglab_final_02_any_root (
  input  [15:0] A,
  input  \input ,
  input  clk,
  input  [3:0] R,
  output [15:0] nroot,
  output busy,
  output [15:0] out_7,
  output [15:0] out_8,
  output [15:0] out_9,
  output [15:0] out_10
);

  wire and_1_out, and_2_out, and_3_out, and_5_out, \break , comparator_1_gt, comparator_2_gt,
       comparator_3_gt, comparator_5_gt, comparator_6_lt, comparator_7_eq, found, multiplexer_12_out,
       multiplexer_13_out, nor_1_out, not_1_out, not_2_out, reset;
  wire [4:0] bitcount_1_out, bitcount_2_out, bitcount_3_out;
  wire [7:0] counter_1_out;
  wire [15:0] add_1_s, div_1_q, mid_2, mid_4, mid_8, multiplexer_1_out, multiplexer_2_out, multiplexer_3_out,
       multiplexer_4_out, multiplexer_5_out, multiplexer_6_out, multiplexer_7_out, multiplexer_8_out,
       multiplexer_9_out, multiplexer_10_out, multiplexer_11_out, sub_1_s;
  wire [31:0] mul_1_mul, mul_2_mul;
  wire [31:16] mid_2_mul, mid_4_mul, mid_8_mul, mul_3_mul;

  Multiplexer #(.Selector_Bits(4), .Bits(16)) multiplexer_1 (
    .sel(R), .in_0(16'h1), .in_1(A), .in_2(16'hff), .in_3(16'h28), .in_4(16'hf), .in_5(16'h9), .in_6(16'h6),
    .in_7(16'h4), .in_8(16'h3), .in_9(16'h3), .in_10(16'h3), .in_11(16'h2), .in_12(16'h2), .in_13(16'h2),
    .in_14(16'h2), .in_15(16'h2), .out(multiplexer_1_out));
  Add #(.Bits(16)) add_1 (.a(out_9), .b(16'h1), .c_i(1'b0), .s(add_1_s));  // open: c_o
  Sub #(.Bits(16)) sub_1 (.a(out_7), .b(out_8), .c_i(1'b0), .s(sub_1_s));  // open: c_o
  Mul #(.Bits(16)) u_mid_2 (.a(out_9), .b(out_9), .mul({mid_2_mul, mid_2}));
  Mul #(.Bits(16)) u_mid_4 (.a(mid_2), .b(mid_2), .mul({mid_4_mul, mid_4}));
  Mul #(.Bits(16)) u_mid_8 (.a(mid_4), .b(mid_4), .mul({mid_8_mul, mid_8}));
  Multiplexer #(.Bits(16)) multiplexer_2 (.sel(found), .in_0(out_9), .in_1(out_7), .out(multiplexer_2_out));
  Multiplexer #(.Bits(16)) multiplexer_3 (.sel(found), .in_0(out_8), .in_1(add_1_s), .out(multiplexer_3_out));
  Div #(.Bits(16)) div_1 (.a(sub_1_s), .b(16'h2), .q(div_1_q));  // open: r
  BitCount #(.Bits(16)) bitcount_1 (.in(mid_2_mul), .out(bitcount_1_out));
  BitCount #(.Bits(16)) bitcount_2 (.in(mid_4_mul), .out(bitcount_2_out));
  BitCount #(.Bits(16)) bitcount_3 (.in(mid_8_mul), .out(bitcount_3_out));
  Multiplexer #(.Bits(16)) multiplexer_4 (
    .sel(reset), .in_0(multiplexer_2_out), .in_1(multiplexer_1_out), .out(multiplexer_4_out));
  Multiplexer #(.Bits(16)) multiplexer_5 (.sel(reset), .in_0(multiplexer_3_out), .in_1(16'h1), .out(multiplexer_5_out));
  Comparator #(.Bits(5)) comparator_1 (.a(bitcount_1_out), .b({5{1'b0}}), .gt(comparator_1_gt));  // open: eq, lt
  Comparator #(.Bits(5)) comparator_2 (.a(bitcount_2_out), .b({5{1'b0}}), .gt(comparator_2_gt));  // open: eq, lt
  Comparator #(.Bits(5)) comparator_3 (.a(bitcount_3_out), .b({5{1'b0}}), .gt(comparator_3_gt));  // open: eq, lt
  D_FF #(.Bits(16)) high (.D(multiplexer_4_out), .C(clk), .Q(out_7));  // open: nQ
  Comparator #(.Bits(16)) comparator_4 (.a(out_8), .b(out_7), .gt(\break ));  // open: eq, lt
  D_FF #(.Bits(16)) low (.D(multiplexer_5_out), .C(clk), .Q(out_8));  // open: nQ
  Add #(.Bits(16)) add_2 (.a(div_1_q), .b(out_8), .c_i(1'b0), .s(out_9));  // open: c_o
  and and_1 (and_1_out, comparator_1_gt, R[1]);
  and and_2 (and_2_out, comparator_2_gt, R[2]);
  and and_3 (and_3_out, comparator_3_gt, R[3]);
  Multiplexer #(.Bits(16)) multiplexer_6 (.sel(R[0]), .in_0(16'h1), .in_1(out_9), .out(multiplexer_6_out));
  Multiplexer #(.Bits(16)) multiplexer_7 (.sel(R[1]), .in_0(16'h1), .in_1(mid_2), .out(multiplexer_7_out));
  Mul #(.Bits(16)) mul_1 (.a(multiplexer_6_out), .b(multiplexer_7_out), .mul(mul_1_mul));
  Multiplexer #(.Bits(16)) multiplexer_8 (.sel(R[2]), .in_0(16'h1), .in_1(mid_4), .out(multiplexer_8_out));
  or or_1 (reset, \input , \break );
  nor nor_1 (nor_1_out, and_1_out, and_2_out, and_3_out);
  Mul #(.Bits(16)) mul_2 (.a(mul_1_mul[15:0]), .b(multiplexer_8_out), .mul(mul_2_mul));
  Multiplexer #(.Bits(16)) multiplexer_9 (.sel(R[3]), .in_0(16'h1), .in_1(mid_8), .out(multiplexer_9_out));
  Comparator #(.Bits(16)) comparator_5 (.a(out_10), .b(A), .gt(comparator_5_gt));  // open: eq, lt
  not not_1 (not_1_out, comparator_5_gt);
  Mul #(.Bits(16)) mul_3 (.a(mul_2_mul[15:0]), .b(multiplexer_9_out), .mul({mul_3_mul, out_10}));
  Comparator #(.Bits(16)) comparator_6 (.a(nroot), .b(out_9), .lt(comparator_6_lt));  // open: gt, eq
  and and_4 (found, nor_1_out, not_1_out);
  and and_5 (and_5_out, comparator_6_lt, not_2_out, found);
  not not_2 (not_2_out, \break );
  Counter #(.Bits(8)) counter_1 (.en(1'b1), .C(clk), .clr(\input ), .out(counter_1_out));  // open: ovf
  Comparator #(.Bits(8)) comparator_7 (.a(counter_1_out), .b(8'hc8), .eq(comparator_7_eq));  // open: gt, lt
  Multiplexer #(.Bits(16)) multiplexer_10 (.sel(and_5_out), .in_0(nroot), .in_1(out_9), .out(multiplexer_10_out));
  Multiplexer #(.Bits(16)) multiplexer_11 (
    .sel(\input ), .in_0(multiplexer_10_out), .in_1({16{1'b0}}), .out(multiplexer_11_out));
  Multiplexer multiplexer_12 (.sel(comparator_7_eq), .in_0(busy), .in_1(1'b0), .out(multiplexer_12_out));
  Multiplexer multiplexer_13 (.sel(\input ), .in_0(multiplexer_12_out), .in_1(1'b1), .out(multiplexer_13_out));
  D_FF #(.Bits(16)) d_ff_1 (.D(multiplexer_11_out), .C(clk), .Q(nroot));  // open: nQ
  D_FF d_ff_2 (.D(multiplexer_13_out), .C(clk), .Q(busy));  // open: nQ

  // Other names for the same wires on the sheet: mid_t[15:0] = out_10; high[15:0] = out_7; low[15:0] = out_8;
  //   mid[15:0] = out_9; R_0 = R[0]; R_1 = R[1]; R_2 = R[2]; R_3 = R[3]

  // Notes on the sheet:
  //   clk: Hz: 200
endmodule

/* Test case TestCase1:
clk A R input nroot busy
0 0 0 0 X 0
1 0 0 0 X 0
0 0 0 0 X 0
1 0 0 0 X 0
0 2 2 1 X X
1 2 2 1 X X
repeat (255) C 2 2 0 X X
0 2 2 0 1 0
1 2 2 0 1 0
0 0 0 0 X 0
1 0 0 0 X 0
0 0 0 0 X 0
1 0 0 0 X 0
0 4 2 1 X X
1 4 2 1 X X
repeat (255) C 4 2 0 X X
0 4 2 0 2 0
1 4 2 0 2 0
0 0 0 0 X 0
1 0 0 0 X 0
0 0 0 0 X 0
1 0 0 0 X 0
0 8 2 1 X X
1 8 2 1 X X
repeat (255) C 8 2 0 X X
0 8 2 0 2 0
1 8 2 0 2 0
0 0 0 0 X 0
1 0 0 0 X 0
0 0 0 0 X 0
1 0 0 0 X 0
0 16 2 1 X X
1 16 2 1 X X
repeat (255) C 16 2 0 X X
0 16 2 0 4 0
1 16 2 0 4 0
*/

/* Test case TestCase4:
clk A R input nroot busy
0 0 0 0 X 0
1 0 0 0 X 0
0 0 0 0 X 0
1 0 0 0 X 0
0 65530 12 1 X X
1 65530 12 1 X X
repeat (255) C 65530 12 0 X X
0 65530 12 0 2 0
1 65530 12 0 2 0
0 0 0 0 X 0
1 0 0 0 X 0
0 0 0 0 X 0
1 0 0 0 X 0
0 60000 3 1 X X
1 60000 3 1 X X
repeat (255) C 60000 3 0 X X
0 60000 3 0 39 0
1 60000 3 0 39 0
0 0 0 0 X 0
1 0 0 0 X 0
0 0 0 0 X 0
1 0 0 0 X 0
0 55124 4 1 X X
1 55124 4 1 X X
repeat (255) C 55124 4 0 X X
0 55124 4 0 15 0
1 55124 4 0 15 0
0 0 0 0 X 0
1 0 0 0 X 0
0 0 0 0 X 0
1 0 0 0 X 0
0 14778 5 1 X X
1 14778 5 1 X X
repeat (255) C 14778 5 0 X X
0 14778 5 0 6 0
1 14778 5 0 6 0
*/

/* Test case TestCase8:
clk A R input nroot busy
0 0 0 0 X 0
1 0 0 0 X 0
0 0 0 0 X 0
1 0 0 0 X 0
0 65535 1 1 X X
1 65535 1 1 X X
repeat (255) C 65535 1 0 X X
0 65535 1 0 65535 0
1 65535 1 0 65535 0
0 0 0 0 X 0
1 0 0 0 X 0
0 0 0 0 X 0
1 0 0 0 X 0
0 64000 15 1 X X
1 64000 15 1 X X
repeat (255) C 64000 15 0 X X
0 64000 15 0 2 0
1 64000 15 0 2 0
0 0 0 0 X 0
1 0 0 0 X 0
0 0 0 0 X 0
1 0 0 0 X 0
0 12000 5 1 X X
1 12000 5 1 X X
repeat (255) C 12000 5 0 X X
0 12000 5 0 6 0
1 12000 5 0 6 0
0 0 0 0 X 0
1 0 0 0 X 0
0 0 0 0 X 0
1 0 0 0 X 0
0 65535 15 1 X X
1 65535 15 1 X X
repeat (255) C 65535 15 0 X X
0 65535 15 0 2 0
1 65535 15 0 2 0
*/
