// Digital circuit diglab_02_02-xor-pos.dig as structural Verilog
module diglab_02_02_xor_pos (
  input  A,
  input  B,
  output Output
);

  wire not_1_out, not_2_out, or_1_out, or_2_out;

  or or_1 (or_1_out, A, B);
  or or_2 (or_2_out, not_1_out, not_2_out);
  not not_1 (not_1_out, A);
  not not_2 (not_2_out, B);
  and and_1 (Output, or_1_out, or_2_out);
endmodule
