// Digital circuit diglab_03_03-cyclic.dig as structural Verilog
module diglab_03_03_cyclic (
  input  v0,
  input  v1,
  input  v2,
  input  v3,
  output a,
  output b,
  output c,
  output d
);

  wire and_2_out, and_3_out, and_4_out, and_5_out, and_6_out, and_7_out, and_8_out, not_1_out, not_2_out,
       not_3_out, not_4_out;

  not not_1 (not_1_out, v0);
  not not_2 (not_2_out, v1);
  not not_3 (not_3_out, v2);
  not not_4 (not_4_out, v3);
  and and_1 (a, v0, not_2_out, not_3_out);
  and and_2 (and_2_out, v0, not_2_out, not_3_out);
  and and_3 (and_3_out, not_1_out, v1);
  and and_4 (and_4_out, not_1_out, not_2_out, v2);
  and and_5 (and_5_out, not_1_out, v1, not_3_out);
  and and_6 (and_6_out, not_1_out, not_3_out, v3);
  and and_7 (and_7_out, not_1_out, v2, not_4_out);
  and and_8 (and_8_out, not_2_out, not_3_out, v3);
  or or_1 (b, and_2_out, and_3_out);
  or or_2 (c, and_4_out, and_5_out);
  or or_3 (d, and_6_out, and_7_out, and_8_out);
endmodule
