// Digital circuit diglab_07_01-simple-memory.dig as structural Verilog
module diglab_07_01_simple_memory (
  input  Load,
  input  A,
  output Z
);

  wire driverinvsel_1_out, not_1_out, not_2_out;

  not not_1 (not_1_out, Load);
  assign driverinvsel_1_out = ~not_1_out ? A : 1'bz;  // DriverInvSel driverinvsel_1
  assign driverinvsel_1_out = ~Load ? Z : 1'bz;  // DriverInvSel driverinvsel_2
  not not_2 (not_2_out, driverinvsel_1_out);
  not not_3 (Z, not_2_out);
endmodule
