// Digital circuit diglab_07_02-rs-latch-nor.dig as structural Verilog
module diglab_07_02_rs_latch_nor (
  input  R,
  input  S,
  output Q,
  output Q_2
);

  nor nor_1 (Q, R, Q_2);
  nor nor_2 (Q_2, Q, S);
endmodule
