// Digital circuit diglab_08_01-counter-74163.dig as structural Verilog
module diglab_08_01_counter_74163 (
  input  P,
  input  T,
  input  D,
  input  C,
  input  B,
  input  A,
  input  Clr,
  input  Load,
  input  Clock,
  output QD,
  output QC,
  output QB,
  output QA,
  output RCO
);

  wire and_1_out;
  wire [3:0] add_1_s, multiplexer_1_out, multiplexer_2_out;

  and and_1 (and_1_out, P, T);
  Add #(.Bits(4)) add_1 (.a({QD, QC, QB, QA}), .b(4'b0000), .c_i(and_1_out), .s(add_1_s), .c_o(RCO));
  Multiplexer #(.Bits(4)) multiplexer_1 (.sel(Clr), .in_0(4'b0000), .in_1(add_1_s), .out(multiplexer_1_out));
  Multiplexer #(.Bits(4)) multiplexer_2 (
    .sel(Load), .in_0({D, C, B, A}), .in_1(multiplexer_1_out), .out(multiplexer_2_out));
  D_FF #(.Bits(4)) d_ff_1 (.D(multiplexer_2_out), .C(Clock), .Q({QD, QC, QB, QA}));  // open: nQ
endmodule
