// Digital circuit diglab_08_02-serial-adder.dig as structural Verilog
module diglab_08_02_serial_adder (
  input  A,
  input  B,
  input  Clr,
  input  Clock,
  output Z
);

  wire add_1_c_o, add_1_s, d_ff_1_q, multiplexer_2_out;

  Add add_1 (.a(A), .b(B), .c_i(d_ff_1_q), .s(add_1_s), .c_o(add_1_c_o));
  Multiplexer multiplexer_1 (.sel(Clr), .in_0(1'b0), .in_1(add_1_s), .out(Z));
  Multiplexer multiplexer_2 (.sel(Clr), .in_0(1'b0), .in_1(add_1_c_o), .out(multiplexer_2_out));
  D_FF d_ff_1 (.D(multiplexer_2_out), .C(Clock), .Q(d_ff_1_q));  // open: nQ
endmodule
