// Digital circuit diglab_08_03-mealy-single-pulser.dig as structural Verilog
module diglab_08_03_mealy_single_pulser (
  input  P,
  input  Clr,
  input  clock,
  output Z
);

  wire and_1_out, and_2_out, d_ff_1_nq, not_1_out;

  and and_1 (and_1_out, P, not_1_out);
  not not_1 (not_1_out, Clr);
  D_FF d_ff_1 (.D(and_1_out), .C(clock), .nQ(d_ff_1_nq));  // open: Q
  and and_2 (and_2_out, and_1_out, d_ff_1_nq);
  D_FF d_ff_2 (.D(and_2_out), .C(clock), .Q(Z));  // open: nQ
endmodule
