// Digital circuit diglab_10_01-sorting.dig as structural Verilog
module diglab_10_01_sorting (
  input  [8:0] N,
  input  reset,
  input  start,
  input  clock,
  output done,
  output [7:0] displayout,
  output [15:0] clockcount,
  output valid
);

  wire multiplexer_1_out;

  Counter counter_1 ();  // open: en, C, clr, out, ovf
  ROM #(.AddrBits(9), .Bits(8)) ROMFILE ();  // open: A, sel, D
  Multiplexer multiplexer_1 (.out(multiplexer_1_out));  // open: sel, in_0, in_1
  Multiplexer multiplexer_2 (.in_0(multiplexer_1_out));  // open: sel, in_1, out
  D_FF d_ff_1 ();  // open: D, C, Q, nQ
  Seven_Seg_Hex seven_seg_hex_1 (.d(displayout[7:4]), .dp(1'b0));
  Seven_Seg_Hex seven_seg_hex_2 (.d(displayout[3:0]), .dp(1'b0));

  // Other names for the same wires on the sheet: clk = clock

  // Notes on the sheet:
  //   clock: Hz: 10
endmodule
