// Digital circuit diglab_10_01-sorting.dig as structural Verilog
module diglab_10_01_sorting (
  input  [8:0] N,
  input  reset,
  input  start,
  input  clock,
  output done,
  output [7:0] displayout,
  output [15:0] clockcount,
  output valid
);

  wire and_3_out, comparator_1_eq, comparator_2_lt, comparator_3_gt, comparator_4_eq, comparator_5_lt,
       comparator_6_eq, comparator_7_gt, comparator_8_gt, comparator_9_lt, d_ff_1_nq, d_ff_2_nq, d_ff_3_q,
       d_ff_4_q, d_ff_5_q, d_ff_6_q, multiplexer_8_out, multiplexer_9_out, multiplexer_12_out,
       multiplexer_14_out, multiplexer_15_out, multiplexer_16_out, multiplexer_17_out, not_1_out, not_2_out,
       not_3_out, not_4_out, reset_t, start_t;
  wire [2:0] multiplexer_1_out, multiplexer_2_out, multiplexer_3_out, multiplexer_4_out, multiplexer_5_out,
       multiplexer_7_out, state;
  wire [7:0] multiplexer_10_out, multiplexer_13_out, rom, value;
  wire [8:0] add_1_s, index, multiplexer_6_out, multiplexer_11_out, ram, sub_1_s;

  Comparator #(.Bits(8)) comparator_1 (.a(value), .b({8{1'b1}}), .eq(comparator_1_eq));  // open: gt, lt
  D_FF d_ff_1 (.D(reset), .C(clock), .nQ(d_ff_1_nq));  // open: Q
  D_FF d_ff_2 (.D(start), .C(clock), .nQ(d_ff_2_nq));  // open: Q
  Multiplexer #(.Bits(3)) multiplexer_1 (.sel(comparator_1_eq), .in_0(3'b010), .in_1(3'b100), .out(multiplexer_1_out));
  D_FF d_ff_3 (.D(reset), .C(clock), .Q(d_ff_3_q));  // open: nQ
  D_FF d_ff_4 (.D(d_ff_1_nq), .C(clock), .Q(d_ff_4_q));  // open: nQ
  D_FF d_ff_5 (.D(start), .C(clock), .Q(d_ff_5_q));  // open: nQ
  D_FF d_ff_6 (.D(d_ff_2_nq), .C(clock), .Q(d_ff_6_q));  // open: nQ
  Comparator #(.Bits(9)) comparator_2 (.a(index), .b(N), .lt(comparator_2_lt));  // open: gt, eq
  Comparator #(.Bits(9)) comparator_3 (.a(ram), .b({9{1'b0}}), .gt(comparator_3_gt));  // open: eq, lt
  and and_1 (reset_t, d_ff_3_q, d_ff_4_q);
  and and_2 (start_t, d_ff_5_q, d_ff_6_q);
  Multiplexer #(.Bits(3)) multiplexer_2 (.sel(start_t), .in_0(3'b000), .in_1(3'b001), .out(multiplexer_2_out));
  Multiplexer #(.Bits(3)) multiplexer_3 (.sel(comparator_2_lt), .in_0(3'b010), .in_1(3'b001), .out(multiplexer_3_out));
  Multiplexer #(.Bits(3)) multiplexer_4 (
    .sel(comparator_3_gt), .in_0(multiplexer_1_out), .in_1(3'b011), .out(multiplexer_4_out));
  Multiplexer #(.Bits(3)) multiplexer_5 (.sel(reset_t), .in_0(3'b100), .in_1(3'b000), .out(multiplexer_5_out));
  ROM #(.AddrBits(9), .isProgramMemory("true"), .Bits(8)) ROMFILE (.A(index), .sel(1'b1), .D(rom));
  Comparator #(.Bits(9)) comparator_4 (.a(ram), .b({9{1'b0}}), .eq(comparator_4_eq));  // open: gt, lt
  Seven_Seg_Hex seven_seg_hex_1 (.d(displayout[7:4]), .dp(1'b0));
  // Probe on rom
  Multiplexer #(.Bits(9)) multiplexer_6 (.sel(comparator_4_eq), .in_0(9'h1), .in_1({9{1'b0}}), .out(multiplexer_6_out));
  Multiplexer #(.Bits(3), .Selector_Bits(3)) multiplexer_7 (
    .sel(state), .in_0(multiplexer_2_out), .in_1(multiplexer_3_out), .in_2(multiplexer_4_out),
    .in_3(multiplexer_4_out), .in_4(multiplexer_5_out), .in_5(3'b000), .in_6(3'b000), .in_7(3'b000),
    .out(multiplexer_7_out));
  D_FF #(.Bits(3)) u_state (.D(multiplexer_7_out), .C(clock), .Q(state));  // open: nQ
  Multiplexer #(.Selector_Bits(3)) multiplexer_8 (
    .sel(state), .in_0(1'b0), .in_1(1'b1), .in_2(1'b0), .in_3(1'b0), .in_4(1'b0), .in_5(1'b0), .in_6(1'b0),
    .in_7(1'b0), .out(multiplexer_8_out));
  Multiplexer #(.Selector_Bits(3)) multiplexer_9 (
    .sel(state), .in_0(1'b1), .in_1(1'b0), .in_2(1'b0), .in_3(1'b0), .in_4(1'b0), .in_5(1'b0), .in_6(1'b0),
    .in_7(1'b0), .out(multiplexer_9_out));
  Seven_Seg_Hex seven_seg_hex_2 (.d(displayout[3:0]), .dp(1'b0));
  // Probe on state
  Counter #(.Bits(9)) u_index (.en(multiplexer_8_out), .C(clock), .clr(multiplexer_9_out), .out(index));  // open: ovf
  Add #(.Bits(9)) add_1 (.a(ram), .b(9'h1), .c_i(1'b0), .s(add_1_s));  // open: c_o
  Sub #(.Bits(9)) sub_1 (.a(ram), .b(multiplexer_6_out), .c_i(1'b0), .s(sub_1_s));  // open: c_o
  Comparator #(.Bits(9)) comparator_5 (.a(index), .b(N), .lt(comparator_5_lt));  // open: gt, eq
  not not_1 (not_1_out, done);
  // Probe on index
  Multiplexer #(.Selector_Bits(3), .Bits(8)) multiplexer_10 (
    .sel(state), .in_0({8{1'b0}}), .in_1(rom), .in_2(value), .in_3(value), .in_4({8{1'b0}}),
    .in_5({8{1'b0}}), .in_6({8{1'b0}}), .in_7({8{1'b0}}), .out(multiplexer_10_out));
  Multiplexer #(.Selector_Bits(3), .Bits(9)) multiplexer_11 (
    .sel(state), .in_0({9{1'b0}}), .in_1(add_1_s), .in_2({9{1'b0}}), .in_3(sub_1_s), .in_4({9{1'b0}}),
    .in_5({9{1'b0}}), .in_6({9{1'b0}}), .in_7({9{1'b0}}), .out(multiplexer_11_out));
  Multiplexer #(.Selector_Bits(3)) multiplexer_12 (
    .sel(state), .in_0(1'b0), .in_1(comparator_5_lt), .in_2(1'b0), .in_3(1'b1), .in_4(1'b0), .in_5(1'b0),
    .in_6(1'b0), .in_7(1'b0), .out(multiplexer_12_out));
  Counter #(.Bits(16)) counter_1 (.en(not_1_out), .C(clock), .clr(start_t), .out(clockcount));  // open: ovf
  Multiplexer #(.Selector_Bits(3), .Bits(8)) multiplexer_13 (
    .sel(state), .in_0({8{1'b0}}), .in_1({8{1'b0}}), .in_2({8{1'b0}}), .in_3(value), .in_4({8{1'b0}}),
    .in_5({8{1'b0}}), .in_6({8{1'b0}}), .in_7({8{1'b0}}), .out(multiplexer_13_out));
  D_FF #(.Bits(8)) u_displayOut (.D(multiplexer_13_out), .C(clock), .Q(displayout));  // open: nQ
  Comparator #(.Bits(8)) comparator_6 (.a(value), .b({8{1'b1}}), .eq(comparator_6_eq));  // open: gt, lt
  Comparator #(.Bits(9)) comparator_7 (.a(ram), .b({9{1'b0}}), .gt(comparator_7_gt));  // open: eq, lt
  RAMDualPort #(.AddrBits(8), .Bits(9)) u_RAM (
    .A(multiplexer_10_out), .Din(multiplexer_11_out), .str(multiplexer_12_out), .C(clock), .ld(1'b1), .D(ram));
  Comparator #(.Bits(9)) comparator_8 (.a(ram), .b({9{1'b0}}), .gt(comparator_8_gt));  // open: eq, lt
  and and_3 (and_3_out, not_2_out, not_3_out);
  not not_2 (not_2_out, comparator_6_eq);
  not not_3 (not_3_out, comparator_7_gt);
  Comparator #(.Bits(9)) comparator_9 (.a(index), .b(N), .lt(comparator_9_lt));  // open: gt, eq
  // Probe on ram
  Multiplexer #(.Selector_Bits(3)) multiplexer_14 (
    .sel(state), .in_0(1'b0), .in_1(1'b0), .in_2(1'b0), .in_3(comparator_8_gt), .in_4(1'b0), .in_5(1'b0),
    .in_6(1'b0), .in_7(1'b0), .out(multiplexer_14_out));
  D_FF u_valid (.D(multiplexer_14_out), .C(clock), .Q(valid));  // open: nQ
  not not_4 (not_4_out, comparator_9_lt);
  Multiplexer #(.Selector_Bits(3)) multiplexer_15 (
    .sel(state), .in_0(1'b0), .in_1(1'b0), .in_2(and_3_out), .in_3(and_3_out), .in_4(1'b0), .in_5(1'b0),
    .in_6(1'b0), .in_7(1'b0), .out(multiplexer_15_out));
  Multiplexer #(.Selector_Bits(3)) multiplexer_16 (
    .sel(state), .in_0(1'b0), .in_1(not_4_out), .in_2(1'b0), .in_3(1'b0), .in_4(1'b0), .in_5(1'b0),
    .in_6(1'b0), .in_7(1'b0), .out(multiplexer_16_out));
  Counter #(.Bits(8)) u_value (.en(multiplexer_15_out), .C(clock), .clr(multiplexer_16_out), .out(value));  // open: ovf
  Multiplexer #(.Selector_Bits(3)) multiplexer_17 (
    .sel(state), .in_0(1'b0), .in_1(1'b0), .in_2(1'b0), .in_3(1'b0), .in_4(1'b1), .in_5(1'b0), .in_6(1'b0),
    .in_7(1'b0), .out(multiplexer_17_out));
  D_FF u_done (.D(multiplexer_17_out), .C(clock), .Q(done));  // open: nQ
  // Probe on value

  // Other names for the same wires on the sheet: clk = clock

  // Notes on the sheet:
  //   clock: Hz: 10
  //   contents of ROMFILE (hex, n*v repeats v):
  //   4*1,3,6,5,1,0,4
endmodule
