// Digital circuit diglab_final_01-counter.dig as structural Verilog
module diglab_final_01_counter (
  input  reset,
  input  clk,
  output A,
  output B,
  output C
);

  wire [2:0] multiplexer_1_out, multiplexer_2_out;

  Multiplexer #(.Bits(3), .Selector_Bits(3)) multiplexer_1 (
    .sel({C, B, A}), .in_0(3'b011), .in_1(3'b100), .in_2(3'b001), .in_3(3'b110), .in_4(3'b111),
    .in_5(3'b010), .in_6(3'b101), .in_7(3'b000), .out(multiplexer_1_out));
  Multiplexer #(.Bits(3)) multiplexer_2 (.sel(reset), .in_0(multiplexer_1_out), .in_1(3'b000), .out(multiplexer_2_out));
  D_FF #(.Bits(3)) d_ff_1 (.D(multiplexer_2_out), .C(clk), .Q({C, B, A}));  // open: nQ
endmodule

/* Test case T1:
clk reset C B A
0 0 0 0 0 
0 1 0 0 0
1 1 0 0 0
0 0 0 0 0
1 0 0 1 1
0 0 0 1 1
1 0 1 1 0
0 0 1 1 0 
1 0 1 0 1
0 0 1 0 1
1 0 0 1 0
0 0 0 1 0
1 0 0 0 1
0 0 0 0 1
1 0 1 0 0
0 0 1 0 0
1 0 1 1 1
0 0 1 1 1
1 0 0 0 0
0 0 0 0 0
1 0 0 1 1
0 0 0 1 1
1 0 1 1 0
0 0 1 1 0 
1 0 1 0 1
0 0 1 0 1
1 0 0 1 0
0 0 0 1 0
1 0 0 0 1
0 0 0 0 1
1 0 1 0 0
0 0 1 0 0
1 0 1 1 1
0 0 1 1 1
*/
