// Digital circuit diglab_final_03-absolute-peak.dig as structural Verilog
module diglab_final_03_absolute_peak (
  input  [15:0] A,
  input  \input ,
  input  clk,
  input  reset,
  output [17:0] peak,
  output [17:0] out_6,
  output [17:0] out_7,
  output [17:0] out_8,
  output [17:0] out_9,
  output [17:0] out_10
);

  wire and_1_out, comparator_1_lt, comparator_2_lt, comparator_3_lt, comparator_4_gt;
  wire [17:0] bitextender_1_out, counter_1_out, multiplexer_1_out, multiplexer_2_out, neg_1_out, neg_2_out,
       sub_1_s, sub_2_s;

  BitExtender #(.inputBits(16), .outputBits(18)) bitextender_1 (.in(A), .out(bitextender_1_out));
  Register #(.Bits(18)) register_1 (.D(bitextender_1_out), .C(clk), .en(\input ), .Q(out_6));
  Sub #(.Bits(18)) sub_1 (.a(out_6), .b(out_7), .c_i(1'b0), .s(sub_1_s));  // open: c_o
  Sub #(.Bits(18)) sub_2 (.a(out_7), .b(out_8), .c_i(1'b0), .s(sub_2_s));  // open: c_o
  Counter #(.Bits(18)) counter_1 (.en(1'b1), .C(\input ), .clr(reset), .out(counter_1_out));  // open: ovf
  Neg #(.Bits(18)) neg_1 (.in(sub_1_s), .out(neg_1_out));
  Comparator #(.Signed("true"), .Bits(18)) comparator_1 (
    .a(sub_1_s), .b({18{1'b0}}), .lt(comparator_1_lt));  // open: gt, eq
  Neg #(.Bits(18)) neg_2 (.in(sub_2_s), .out(neg_2_out));
  Comparator #(.Signed("true"), .Bits(18)) comparator_2 (
    .a(sub_2_s), .b({18{1'b0}}), .lt(comparator_2_lt));  // open: gt, eq
  Comparator #(.Signed("true"), .Bits(18)) comparator_3 (.a(out_10), .b(out_9), .lt(comparator_3_lt));  // open: gt, eq
  Comparator #(.Signed("true"), .Bits(18)) comparator_4 (
    .a(counter_1_out), .b(18'h2), .gt(comparator_4_gt));  // open: eq, lt
  Multiplexer #(.Bits(18)) multiplexer_1 (
    .sel(comparator_1_lt), .in_0(sub_1_s), .in_1(neg_1_out), .out(multiplexer_1_out));
  Multiplexer #(.Bits(18)) multiplexer_2 (
    .sel(comparator_2_lt), .in_0(sub_2_s), .in_1(neg_2_out), .out(multiplexer_2_out));
  Register #(.Bits(18)) register_2 (.D(out_6), .C(clk), .en(\input ), .Q(out_7));
  Add #(.Bits(18)) add_1 (.a(multiplexer_1_out), .b(multiplexer_2_out), .c_i(1'b0), .s(out_9));  // open: c_o
  and and_1 (and_1_out, comparator_3_lt, comparator_4_gt);
  Register #(.Bits(18)) register_3 (.D(out_9), .C(~clk), .en(and_1_out), .Q(out_10));
  Register #(.Bits(18)) register_4 (.D(out_7), .C(clk), .en(\input ), .Q(out_8));

  assign peak = out_10;

  // Other names for the same wires on the sheet: a_t[17:0] = out_6; b[17:0] = out_7; c[17:0] = out_8;
  //   result[17:0] = out_10; tmp[17:0] = out_9

  // Notes on the sheet:
  //   clk: Hz: 200
endmodule

/* Test case Testcase1:
clk A input reset peak
0 0 0 0 0
1 0 0 0 0
0 0 0 1 0
1 0 0 1 0
0 0  0 0 0
1 0  0 0 0
0 5 1 0 X
1 5 1 0 X
0 0 0 0 X
1 0 0 0 X
0 1 1 0 X
1 1 1 0 X
0 0 0 0 X
1 0 0 0 X
0 0 0 0 X
1 0 0 0 X
0 2 1 0 X
1 2 1 0 X
0 0 0 0 X
1 0 0 0 X
0  0 0 0 5
1  0 0 0 5
0 10 1 0 X
1 10 1 0 X
0 0 0 0 X
1 0 0 0 9
0  0 0 0 9
1  0 0 0 9
0 3 1 0 X
1 3 1 0 X
0 0 0 0 X
1 0 0 0 15
0  0 0 0 15
1  0 0 0 15
0 65526 1 0 X
1 65526 1 0 X
0 0 0 0 X
1 0 0 0 20
0  0 0 0 20
1  0 0 0 20
0 2 1 0 X
1 2 1 0 X
0 0 0 0 X
1 0 0 0 25
0  0 0 0 25
1  0 0 0 25
0 4 1 0 X
1 4 1 0 X
0 0 0 0 X
1 0 0 0 25
0  0 0 0 25
1  0 0 0 25
0 1 1 0 X
1 1 1 0 X
0 0 0 0 X
1 0 0 0 25
0  0 0 0 25
1  0 0 0 25
0 2 1 0 X
1 2 1 0 X
0 0 0 0 X
1 0 0 0 25
*/

/* Test case Testcase3:
clk A input reset peak
0 0 0 0 0
1 0 0 0 0
0 0 0 1 0
1 0 0 1 0
0 0  0 0 0
1 0  0 0 0
0 9924 1 0 X
1 9924 1 0 X
0 0 0 0 X
1 0 0 0 X
0 1714 1 0 X
1 1714 1 0 X
0 0 0 0 X
1 0 0 0 X
0 0 0 0 X
1 0 0 0 X
0 19734 1 0 X
1 19734 1 0 X
0 0 0 0 X
1 0 0 0 X
0  0 0 0 26230
1  0 0 0 26230
0 14144 1 0 X
1 14144 1 0 X
0 0 0 0 X
1 0 0 0 26230
0  0 0 0 26230
1  0 0 0 26230
0 6348 1 0 X
1 6348 1 0 X
0 0 0 0 X
1 0 0 0 26230
0  0 0 0 26230
1  0 0 0 26230
0 29200 1 0 X
1 29200 1 0 X
0 0 0 0 X
1 0 0 0 30648
0  0 0 0 30648
1  0 0 0 30648
0 13658 1 0 X
1 13658 1 0 X
0 0 0 0 X
1 0 0 0 38394
0  0 0 0 38394
1  0 0 0 38394
0 20001 1 0 X
1 20001 1 0 X
0 0 0 0 X
1 0 0 0 38394
0  0 0 0 38394
1  0 0 0 38394
0 23323 1 0 X
1 23323 1 0 X
0 0 0 0 X
1 0 0 0 38394
0  0 0 0 38394
1  0 0 0 38394
0 15516 1 0 X
1 15516 1 0 X
0 0 0 0 X
1 0 0 0 38394
0  0 0 0 38394
1  0 0 0 38394
0 26104 1 0 X
1 26104 1 0 X
0 0 0 0 X
1 0 0 0 38394
0  0 0 0 38394
1  0 0 0 38394
0 23576 1 0 X
1 23576 1 0 X
0 0 0 0 X
1 0 0 0 38394
0  0 0 0 38394
1  0 0 0 38394
0 15152 1 0 X
1 15152 1 0 X
0 0 0 0 X
1 0 0 0 38394
0  0 0 0 38394
1  0 0 0 38394
0 9762 1 0 X
1 9762 1 0 X
0 0 0 0 X
1 0 0 0 38394
0  0 0 0 38394
1  0 0 0 38394
0 3599 1 0 X
1 3599 1 0 X
0 0 0 0 X
1 0 0 0 38394
0  0 0 0 38394
1  0 0 0 38394
0 16576 1 0 X
1 16576 1 0 X
0 0 0 0 X
1 0 0 0 38394
0  0 0 0 38394
1  0 0 0 38394
0 30162 1 0 X
1 30162 1 0 X
0 0 0 0 X
1 0 0 0 38394
0  0 0 0 38394
1  0 0 0 38394
0 30934 1 0 X
1 30934 1 0 X
0 0 0 0 X
1 0 0 0 38394
0  0 0 0 38394
1  0 0 0 38394
0 31029 1 0 X
1 31029 1 0 X
0 0 0 0 X
1 0 0 0 38394
0  0 0 0 38394
1  0 0 0 38394
0 18783 1 0 X
1 18783 1 0 X
0 0 0 0 X
1 0 0 0 38394
0  0 0 0 38394
1  0 0 0 38394
0 1881 1 0 X
1 1881 1 0 X
0 0 0 0 X
1 0 0 0 38394
0  0 0 0 38394
1  0 0 0 38394
0 10695 1 0 X
1 10695 1 0 X
0 0 0 0 X
1 0 0 0 38394
0  0 0 0 38394
1  0 0 0 38394
0 7756 1 0 X
1 7756 1 0 X
0 0 0 0 X
1 0 0 0 38394
0  0 0 0 38394
1  0 0 0 38394
0 14129 1 0 X
1 14129 1 0 X
0 0 0 0 X
1 0 0 0 38394
0  0 0 0 38394
1  0 0 0 38394
0 30596 1 0 X
1 30596 1 0 X
0 0 0 0 X
1 0 0 0 38394
0  0 0 0 38394
1  0 0 0 38394
0 21070 1 0 X
1 21070 1 0 X
0 0 0 0 X
1 0 0 0 38394
0  0 0 0 38394
1  0 0 0 38394
0 15427 1 0 X
1 15427 1 0 X
0 0 0 0 X
1 0 0 0 38394
0  0 0 0 38394
1  0 0 0 38394
0 2565 1 0 X
1 2565 1 0 X
0 0 0 0 X
1 0 0 0 38394
0  0 0 0 38394
1  0 0 0 38394
0 24554 1 0 X
1 24554 1 0 X
0 0 0 0 X
1 0 0 0 38394
0  0 0 0 38394
1  0 0 0 38394
0 25370 1 0 X
1 25370 1 0 X
0 0 0 0 X
1 0 0 0 38394
0  0 0 0 38394
1  0 0 0 38394
0 9273 1 0 X
1 9273 1 0 X
0 0 0 0 X
1 0 0 0 38394
0  0 0 0 38394
1  0 0 0 38394
0 8302 1 0 X
1 8302 1 0 X
0 0 0 0 X
1 0 0 0 38394
0  0 0 0 38394
1  0 0 0 38394
0 3282 1 0 X
1 3282 1 0 X
0 0 0 0 X
1 0 0 0 38394
0  0 0 0 38394
1  0 0 0 38394
0 25633 1 0 X
1 25633 1 0 X
0 0 0 0 X
1 0 0 0 38394
0  0 0 0 38394
1  0 0 0 38394
0 13448 1 0 X
1 13448 1 0 X
0 0 0 0 X
1 0 0 0 38394
0  0 0 0 38394
1  0 0 0 38394
0 5516 1 0 X
1 5516 1 0 X
0 0 0 0 X
1 0 0 0 38394
0  0 0 0 38394
1  0 0 0 38394
0 31976 1 0 X
1 31976 1 0 X
0 0 0 0 X
1 0 0 0 38394
0  0 0 0 38394
1  0 0 0 38394
0 24271 1 0 X
1 24271 1 0 X
0 0 0 0 X
1 0 0 0 38394
0  0 0 0 38394
1  0 0 0 38394
0 6215 1 0 X
1 6215 1 0 X
0 0 0 0 X
1 0 0 0 38394
0  0 0 0 38394
1  0 0 0 38394
0 10282 1 0 X
1 10282 1 0 X
0 0 0 0 X
1 0 0 0 38394
0  0 0 0 38394
1  0 0 0 38394
0 28448 1 0 X
1 28448 1 0 X
0 0 0 0 X
1 0 0 0 38394
0  0 0 0 38394
1  0 0 0 38394
0 19282 1 0 X
1 19282 1 0 X
0 0 0 0 X
1 0 0 0 38394
0  0 0 0 38394
1  0 0 0 38394
0 16410 1 0 X
1 16410 1 0 X
0 0 0 0 X
1 0 0 0 38394
0  0 0 0 38394
1  0 0 0 38394
0 4699 1 0 X
1 4699 1 0 X
0 0 0 0 X
1 0 0 0 38394
0  0 0 0 38394
1  0 0 0 38394
0 17855 1 0 X
1 17855 1 0 X
0 0 0 0 X
1 0 0 0 38394
0  0 0 0 38394
1  0 0 0 38394
0 7295 1 0 X
1 7295 1 0 X
0 0 0 0 X
1 0 0 0 38394
0  0 0 0 38394
1  0 0 0 38394
0 5567 1 0 X
1 5567 1 0 X
0 0 0 0 X
1 0 0 0 38394
0  0 0 0 38394
1  0 0 0 38394
0 5318 1 0 X
1 5318 1 0 X
0 0 0 0 X
1 0 0 0 38394
0  0 0 0 38394
1  0 0 0 38394
0 7523 1 0 X
1 7523 1 0 X
0 0 0 0 X
1 0 0 0 38394
0  0 0 0 38394
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*/

/* Test case Testcase6:
clk A input reset peak
0 0 0 0 0
1 0 0 0 0
0 0 0 1 0
1 0 0 1 0
0 0  0 0 0
1 0  0 0 0
0 64563 1 0 X
1 64563 1 0 X
0 0 0 0 X
1 0 0 0 X
0 64536 1 0 X
1 64536 1 0 X
0 0 0 0 X
1 0 0 0 X
0 0 0 0 X
1 0 0 0 X
0 64709 1 0 X
1 64709 1 0 X
0 0 0 0 X
1 0 0 0 X
0  0 0 0 200
1  0 0 0 200
0 64724 1 0 X
1 64724 1 0 X
0 0 0 0 X
1 0 0 0 200
0  0 0 0 200
1  0 0 0 200
0 64709 1 0 X
1 64709 1 0 X
0 0 0 0 X
1 0 0 0 200
0  0 0 0 200
1  0 0 0 200
0 64804 1 0 X
1 64804 1 0 X
0 0 0 0 X
1 0 0 0 200
0  0 0 0 200
1  0 0 0 200
0 64890 1 0 X
1 64890 1 0 X
0 0 0 0 X
1 0 0 0 200
0  0 0 0 200
1  0 0 0 200
0 64804 1 0 X
1 64804 1 0 X
0 0 0 0 X
1 0 0 0 200
0  0 0 0 200
1  0 0 0 200
0 64917 1 0 X
1 64917 1 0 X
0 0 0 0 X
1 0 0 0 200
0  0 0 0 200
1  0 0 0 200
0 64968 1 0 X
1 64968 1 0 X
0 0 0 0 X
1 0 0 0 200
0  0 0 0 200
1  0 0 0 200
0 64917 1 0 X
1 64917 1 0 X
0 0 0 0 X
1 0 0 0 200
0  0 0 0 200
1  0 0 0 200
0 65085 1 0 X
1 65085 1 0 X
0 0 0 0 X
1 0 0 0 219
0  0 0 0 219
1  0 0 0 219
0 65153 1 0 X
1 65153 1 0 X
0 0 0 0 X
1 0 0 0 236
0  0 0 0 236
1  0 0 0 236
0 65085 1 0 X
1 65085 1 0 X
0 0 0 0 X
1 0 0 0 236
0  0 0 0 236
1  0 0 0 236
0 65242 1 0 X
1 65242 1 0 X
0 0 0 0 X
1 0 0 0 236
0  0 0 0 236
1  0 0 0 236
0 65299 1 0 X
1 65299 1 0 X
0 0 0 0 X
1 0 0 0 236
0  0 0 0 236
1  0 0 0 236
0 65242 1 0 X
1 65242 1 0 X
0 0 0 0 X
1 0 0 0 236
0  0 0 0 236
1  0 0 0 236
0 65411 1 0 X
1 65411 1 0 X
0 0 0 0 X
1 0 0 0 236
0  0 0 0 236
1  0 0 0 236
0 65453 1 0 X
1 65453 1 0 X
0 0 0 0 X
1 0 0 0 236
0  0 0 0 236
1  0 0 0 236
0 65411 1 0 X
1 65411 1 0 X
0 0 0 0 X
1 0 0 0 236
0  0 0 0 236
1  0 0 0 236
0 152 1 0 X
1 152 1 0 X
0 0 0 0 X
1 0 0 0 319
0  0 0 0 319
1  0 0 0 319
0 175 1 0 X
1 175 1 0 X
0 0 0 0 X
1 0 0 0 319
0  0 0 0 319
1  0 0 0 319
0 152 1 0 X
1 152 1 0 X
0 0 0 0 X
1 0 0 0 319
0  0 0 0 319
1  0 0 0 319
0 546 1 0 X
1 546 1 0 X
0 0 0 0 X
1 0 0 0 417
0  0 0 0 417
1  0 0 0 417
0 612 1 0 X
1 612 1 0 X
0 0 0 0 X
1 0 0 0 460
0  0 0 0 460
1  0 0 0 460
0 546 1 0 X
1 546 1 0 X
0 0 0 0 X
1 0 0 0 460
0  0 0 0 460
1  0 0 0 460
0 947 1 0 X
1 947 1 0 X
0 0 0 0 X
1 0 0 0 467
0  0 0 0 467
1  0 0 0 467
0 1033 1 0 X
1 1033 1 0 X
0 0 0 0 X
1 0 0 0 487
0  0 0 0 487
1  0 0 0 487
0 947 1 0 X
1 947 1 0 X
0 0 0 0 X
1 0 0 0 487
0  0 0 0 487
1  0 0 0 487
0 1335 1 0 X
1 1335 1 0 X
0 0 0 0 X
1 0 0 0 487
0  0 0 0 487
1  0 0 0 487
0 1351 1 0 X
1 1351 1 0 X
0 0 0 0 X
1 0 0 0 487
0  0 0 0 487
1  0 0 0 487
0 1335 1 0 X
1 1335 1 0 X
0 0 0 0 X
1 0 0 0 487
0  0 0 0 487
1  0 0 0 487
0 1847 1 0 X
1 1847 1 0 X
0 0 0 0 X
1 0 0 0 528
0  0 0 0 528
1  0 0 0 528
0 1884 1 0 X
1 1884 1 0 X
0 0 0 0 X
1 0 0 0 549
0  0 0 0 549
1  0 0 0 549
0 1847 1 0 X
1 1847 1 0 X
0 0 0 0 X
1 0 0 0 549
0  0 0 0 549
1  0 0 0 549
0 2409 1 0 X
1 2409 1 0 X
0 0 0 0 X
1 0 0 0 599
0  0 0 0 599
1  0 0 0 599
0 2440 1 0 X
1 2440 1 0 X
0 0 0 0 X
1 0 0 0 599
0  0 0 0 599
1  0 0 0 599
0 2409 1 0 X
1 2409 1 0 X
0 0 0 0 X
1 0 0 0 599
0  0 0 0 599
1  0 0 0 599
0 3004 1 0 X
1 3004 1 0 X
0 0 0 0 X
1 0 0 0 626
0  0 0 0 626
1  0 0 0 626
0 3099 1 0 X
1 3099 1 0 X
0 0 0 0 X
1 0 0 0 690
0  0 0 0 690
1  0 0 0 690
0 3004 1 0 X
1 3004 1 0 X
0 0 0 0 X
1 0 0 0 690
0  0 0 0 690
1  0 0 0 690
0 3576 1 0 X
1 3576 1 0 X
0 0 0 0 X
1 0 0 0 690
0  0 0 0 690
1  0 0 0 690
0 3581 1 0 X
1 3581 1 0 X
0 0 0 0 X
1 0 0 0 690
0  0 0 0 690
1  0 0 0 690
0 3576 1 0 X
1 3576 1 0 X
0 0 0 0 X
1 0 0 0 690
0  0 0 0 690
1  0 0 0 690
0 4285 1 0 X
1 4285 1 0 X
0 0 0 0 X
1 0 0 0 714
0  0 0 0 714
1  0 0 0 714
0 4345 1 0 X
1 4345 1 0 X
0 0 0 0 X
1 0 0 0 769
0  0 0 0 769
1  0 0 0 769
0 4285 1 0 X
1 4285 1 0 X
0 0 0 0 X
1 0 0 0 769
0  0 0 0 769
1  0 0 0 769
0 4982 1 0 X
1 4982 1 0 X
0 0 0 0 X
1 0 0 0 769
0  0 0 0 769
1  0 0 0 769
0 5014 1 0 X
1 5014 1 0 X
0 0 0 0 X
1 0 0 0 769
0  0 0 0 769
1  0 0 0 769
0 4982 1 0 X
1 4982 1 0 X
0 0 0 0 X
1 0 0 0 769
0  0 0 0 769
1  0 0 0 769
0 5798 1 0 X
1 5798 1 0 X
0 0 0 0 X
1 0 0 0 848
0  0 0 0 848
1  0 0 0 848
0 5852 1 0 X
1 5852 1 0 X
0 0 0 0 X
1 0 0 0 870
0  0 0 0 870
1  0 0 0 870
0 5798 1 0 X
1 5798 1 0 X
0 0 0 0 X
1 0 0 0 870
0  0 0 0 870
1  0 0 0 870
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*/
