// Digital circuit diglab_midterm_01.dig as structural Verilog
module diglab_midterm_01 (
  input  a0,
  input  a1,
  input  a2,
  input  b0,
  input  b1,
  input  b2,
  output o
);

  wire decoder_1_out_10, decoder_1_out_11, decoder_1_out_12, decoder_1_out_13, decoder_1_out_14,
       decoder_1_out_15;
  wire [3:0] add_1_s;

  Add #(.Bits(4)) add_1 (.a({1'b0, a2, a1, a0}), .b({1'b0, b2, b1, b0}), .c_i(1'b0), .s(add_1_s));  // open: c_o
  or or_1 (o, decoder_1_out_10, decoder_1_out_11, decoder_1_out_12, decoder_1_out_13, decoder_1_out_14, decoder_1_out_15);
  Seven_Seg_Hex seven_seg_hex_1 (.d({3'b000, o}), .dp(1'b0));
  Decoder #(.Selector_Bits(4)) decoder_1 (
    .sel(add_1_s), .out_10(decoder_1_out_10), .out_11(decoder_1_out_11), .out_12(decoder_1_out_12),
    .out_13(decoder_1_out_13), .out_14(decoder_1_out_14), .out_15(decoder_1_out_15));  // open: out_0, out_1, out_2, out_3, out_4, out_5, out_6, out_7, out_8, out_9
endmodule

/* Test case:
a2	a1	a0	b2	b1	b0	o
0	0	0	0	0	0	0
0	0	0	0	0	1	0
0	0	0	0	1	0	0
0	0	0	0	1	1	0
0	0	0	1	0	0	0
0	0	0	1	0	1	0
0	0	0	1	1	0	0
0	0	0	1	1	1	0
0	0	1	0	0	0	0
0	0	1	0	0	1	0
0	0	1	0	1	0	0
0	0	1	0	1	1	0
0	0	1	1	0	0	0
0	0	1	1	0	1	0
0	0	1	1	1	0	0
0	0	1	1	1	1	0
0	1	0	0	0	0	0
0	1	0	0	0	1	0
0	1	0	0	1	0	0
0	1	0	0	1	1	0
0	1	0	1	0	0	0
0	1	0	1	0	1	0
0	1	0	1	1	0	0
0	1	0	1	1	1	0
0	1	1	0	0	0	0
0	1	1	0	0	1	0
0	1	1	0	1	0	0
0	1	1	0	1	1	0
0	1	1	1	0	0	0
0	1	1	1	0	1	0
0	1	1	1	1	0	0
0	1	1	1	1	1	1
1	0	0	0	0	0	0
1	0	0	0	0	1	0
1	0	0	0	1	0	0
1	0	0	0	1	1	0
1	0	0	1	0	0	0
1	0	0	1	0	1	0
1	0	0	1	1	0	1
1	0	0	1	1	1	1
1	0	1	0	0	0	0
1	0	1	0	0	1	0
1	0	1	0	1	0	0
1	0	1	0	1	1	0
1	0	1	1	0	0	0
1	0	1	1	0	1	1
1	0	1	1	1	0	1
1	0	1	1	1	1	1
1	1	0	0	0	0	0
1	1	0	0	0	1	0
1	1	0	0	1	0	0
1	1	0	0	1	1	0
1	1	0	1	0	0	1
1	1	0	1	0	1	1
1	1	0	1	1	0	1
1	1	0	1	1	1	1
1	1	1	0	0	0	0
1	1	1	0	0	1	0
1	1	1	0	1	0	0
1	1	1	0	1	1	1
1	1	1	1	0	0	1
1	1	1	1	0	1	1
1	1	1	1	1	0	1
1	1	1	1	1	1	1
*/
