// Digital circuit diglab_midterm_02.dig as structural Verilog
module diglab_midterm_02 (
  input  s2,
  input  s1,
  input  s0
);

  wire decoder_1_out_2, decoder_1_out_4, decoder_1_out_5, decoder_1_out_6, decoder_2_out_0, decoder_2_out_2,
       decoder_2_out_4, decoder_2_out_6, decoder_2_out_7, or_1_out, or_2_out;

  Decoder #(.Selector_Bits(3)) decoder_1 (
    .sel({s0, s1, s2}), .out_2(decoder_1_out_2), .out_4(decoder_1_out_4), .out_5(decoder_1_out_5),
    .out_6(decoder_1_out_6));  // open: out_0, out_1, out_3, out_7
  or or_1 (or_1_out, decoder_1_out_2, decoder_1_out_4, decoder_1_out_5, decoder_1_out_6);
  // Probe on or_1_out
  Decoder #(.Selector_Bits(3)) decoder_2 (
    .sel({s0, s1, s2}), .out_0(decoder_2_out_0), .out_2(decoder_2_out_2), .out_4(decoder_2_out_4),
    .out_6(decoder_2_out_6), .out_7(decoder_2_out_7));  // open: out_1, out_3, out_5
  or or_2 (or_2_out, decoder_2_out_0, decoder_2_out_2, decoder_2_out_4, decoder_2_out_6, decoder_2_out_7);
  // Probe on or_2_out
endmodule

/* Test case:
s0 s1 s2 o1 o2
0 0 0 0 1
0 0 1 0 0
0 1 0 1 1
0 1 1 0 0
1 0 0 1 1
1 0 1 1 0
1 1 0 1 1
1 1 1 0 1
*/
